# Fritzing sketch ControleCapacitivo (saved by Fritzing 0.9.2b)
breadboards: 1

parts:
  Componente1 = Arduino Uno (Rev3)
  S1 = Pushbutton [package="[THT]"]
  S2 = Pushbutton [package="[THT]"]
  R1 = Resistor [tolerance=±5% resistance=5M package=THT]
  C1 = Ceramic Capacitor [capacitance=100nF package="100 mil [THT, multilayer]"]
  C2 = Ceramic Capacitor [capacitance=100nF package="100 mil [THT, multilayer]"]
  R2 = Resistor [tolerance=±5% resistance=5M package=THT]
  R3 = Resistor [tolerance=±5% resistance=5M package=THT]
  C3 = Ceramic Capacitor [capacitance=100nF package="100 mil [THT, multilayer]"]
  R4 = Resistor [tolerance=±5% resistance=5M package=THT]
  C4 = Ceramic Capacitor [capacitance=100nF package="100 mil [THT, multilayer]"]
  R5 = Resistor [tolerance=±5% resistance=5M package=THT]
  C5 = Ceramic Capacitor [capacitance=100nF package="100 mil [THT, multilayer]"]
  R6 = Resistor [tolerance=±5% resistance=5M package=THT]
  C6 = Ceramic Capacitor [capacitance=100nF package="100 mil [THT, multilayer]"]
  S3 = Tilt Switch [package=THT]
  S4 = Tilt Switch [package=THT]
  S5 = Tilt Switch [package=THT]
  S6 = Tilt Switch [package=THT]
  S7 = Tilt Switch [package=THT]
  S8 = Tilt Switch [package=THT]

nets:
  N1: Componente1.D8, R1.Pin_1, R2.Pin_1, R3.Pin_1, R4.Pin_1, R5.Pin_1, R6.Pin_1
  N2: Componente1.D10_PWM/SS, S2.Pin_3, S2.Pin_4
  N3: Componente1.D11_PWM/MOSI, S1.Pin_3, S1.Pin_4
  N4: Componente1.D2, R1.Pin_0, C1.0, S3.Pin_2
  N5: Componente1.D3_PWM, C2.0, R2.Pin_0, S4.Pin_2
  N6: Componente1.D4, R3.Pin_0, C3.0, S5.Pin_2
  N7: Componente1.D5_PWM, R4.Pin_0, C4.0, S8.Pin_1
  N8: Componente1.D6_PWM, R5.Pin_0, C5.0, S7.Pin_1
  N9: Componente1.D7, R6.Pin_0, C6.0, S6.Pin_1
  N10: Componente1.GND, S1.Pin_1, S1.Pin_2, S2.Pin_1, S2.Pin_2, C1.1, C2.1, C3.1, C4.1, C5.1, C6.1

notes:
  Sensor da porta 2
  Sensor da porta 3
  Sensor da porta 4
  Sensor da porta 7
  Sensor da porta 6
  Sensor da porta 5
  Botões de start e hotkey

// code stored in the sketch: PsBanana.ino
#include "UnoJoy.h"
#include <CapacitiveSensor.h>
const int resolution = 10;
const long sensitivity = 2300;
const long sensitivity2 = 2700;
CapacitiveSensor cs[] = {
  CapacitiveSensor(8, 2),
  CapacitiveSensor(8, 3),
  CapacitiveSensor(8, 4),
  CapacitiveSensor(8, 5), 
  CapacitiveSensor(8, 6),
  CapacitiveSensor(8, 7),
};
const int NUMBER_OF_SENSORS = 6;
long timeArr[NUMBER_OF_SENSORS];

void setup(){
  for (int i = 0; i++; i < NUMBER_OF_SENSORS) {
    timeArr[i] = 0;
    cs[i].set_CS_AutocaL_Millis(0xFFFFFFFF);
  }
  setupUnoJoy();// Inicializa as funções do UnoJoy
  pinMode(11, INPUT_PULLUP);
  pinMode(10, INPUT_PULLUP);
}

void loop(){
  // Sempre fica atualizando o dado a ser enviado ao computador
  dataForController_t controllerData = getControllerData();
  setControllerData(controllerData);
}

dataForController_t getControllerData(void){  
  //  Configura local onde dados do controle são armazenados
  //  Serve para limpar o buffer onde os dados do controle são armazenados
  dataForController_t controllerData = getBlankDataForController();

  controllerData.dpadDownOn = (cs[0].capacitiveSensor(resolution) > sensitivity);
  controllerData.dpadLeftOn = (cs[1].capacitiveSensor(resolution) > sensitivity);
  controllerData.dpadUpOn = (cs[2].capacitiveSensor(resolution) > sensitivity);
  controllerData.dpadRightOn = (cs[3].capacitiveSensor(resolution) > sensitivity);
  controllerData.crossOn = (cs[4].capacitiveSensor(resolution) > sensitivity2);
  controllerData.triangleOn = (cs[5].capacitiveSensor(resolution) > sensitivity);
  controllerData.startOn = !digitalRead(11);
  controllerData.selectOn = !digitalRead(10);

  return controllerData;
}
